# Fritzing sketch Wiring (saved by Fritzing 0.9.3b)
breadboards: 1

parts:
  YL-1 = YL-38 Humitidy Sensor
  DHT1 = DHT22 Humidity and Temperature Sensor
  IC1 = MCP3008 8-channel 10-bit ADC [part_number=MCP3008]
  Raspberry_Pi_1 = Raspberry Pi 3 [part_number=RPI-3-V1.2]
  R1 = Resistor [tolerance=±5% resistance=10k package=THT]
  R2 = Resistor [tolerance=±5% resistance=220 package=THT]
  LED1 = LED - 5mm [color="Red (633nm)" package="5 mm [THT]"]

nets:
  VCC: YL-1.VCC, DHT1.VDD, Raspberry_Pi_1.3v3, R1.Pin_1
  GND: YL-1.GND, DHT1.GND, Raspberry_Pi_1.GND, LED1.cathode
  N1: YL-1.ANALOG, IC1.no_name_yet#1
  N2: DHT1.DATA, Raspberry_Pi_1.GPIO2, R1.Pin_0
  N3: Raspberry_Pi_1.GPIO25, R2.Pin_1
  N4: R2.Pin_0, LED1.anode
